# Fritzing sketch Wiring Diagram (saved by Fritzing 1.0.5)
breadboards: 2

parts:
  IC1 = IC, DIP package, 16 pins [chip_label=MAX31865]
  IC2 = IC, DIP package, 16 pins [chip_label=MAX31865]
  IC3 = IC, DIP package, 16 pins [chip_label=MAX31865]
  IC4 = IC, DIP package, 16 pins [chip_label=MAX31865]
  IC5 = IC, DIP package, 16 pins [chip_label=MAX31865]
  Part2 = Arduino Leonardo (Rev3b)
  IC6 = IC, DIP package, 16 pins [chip_label=DRV8825]
  Power_plug1 = Power plug
  M1 = Stepper Motor - Bipolar
  IC7 = IC, DIP package, 8 pins [chip_label=RYLR998]
  U1 = LCD-16X2 [package=lcd-16x2]  # not connected
  S1 = Pushbutton [package="[THT]"]
  S2 = Pushbutton [package="[THT]"]
  R1 = Resistor [tolerance=±5% power=0.25W resistance=220 package=THT]
  R2 = Resistor [tolerance=±5% power=0.25W resistance=220 package=THT]

nets:
  N1: IC1.pin1, IC2.pin1, IC3.pin1, IC4.pin1, IC5.pin1, Part2.3V3, IC6.pin5, IC6.pin6, IC7.pin4
  N2: IC1.pin2, IC2.pin2, IC3.pin2, IC4.pin2, IC5.pin2, Part2.GND, IC6.pin9, IC7.pin1, R2.Pin_1
  N3: IC1.pin4, IC2.pin4, IC3.pin4, IC4.pin4, IC5.pin4, Part2.D13_PWM
  N4: IC1.pin5, IC2.pin5, IC3.pin5, IC4.pin5, IC5.pin5, Part2.D12/A11
  N5: IC1.pin6, IC2.pin6, IC3.pin6, IC4.pin6, IC5.pin6, Part2.D11_PWM
  N6: IC1.pin7, Part2.D10_PWM/A10
  N7: IC1.pin10, IC1.pin11, IC1.pin12, IC1.pin13, IC1.pin14, IC2.pin9, IC2.pin10, IC2.pin11, IC2.pin13, IC2.pin14, IC2.pin15, IC2.pin16, IC3.pin10, IC3.pin11, IC3.pin12, IC3.pin13, IC3.pin14, IC3.pin16, IC4.pin9, IC4.pin10, IC4.pin11, IC4.pin13, IC4.pin14, IC4.pin15, IC4.pin16, IC5.pin10, IC5.pin11, IC5.pin12, IC5.pin13, IC5.pin14, IC5.pin16, IC6.pin16, Power_plug1.GND
  N8: IC2.pin7, Part2.D9_PWM/A9
  N9: IC3.pin7, Part2.D8/A8
  N10: IC4.pin7, Part2.D7
  N11: IC5.pin7, Part2.D6_PWM/A7
  N12: Part2.D0/RX, IC7.pin2
  N13: Part2.D1/TX, IC7.pin3
  N14: Part2.D2/SDA, Part2.SDA, IC6.pin8
  N15: Part2.D3_PWM/SCL, Part2.SCL, IC6.pin7
  N16: Part2.A3, S1.Pin_3, S1.Pin_4, S2.Pin_3, S2.Pin_4
  N17: IC6.pin11, M1.D
  N18: IC6.pin12, M1.B
  N19: IC6.pin13, M1.C
  N20: IC6.pin14, M1.A
  N21: IC6.pin15, Power_plug1.VCC
  N22: S1.Pin_1, S1.Pin_2, R1.Pin_0
  N23: S2.Pin_1, S2.Pin_2, R1.Pin_1, R2.Pin_0
